# Fritzing sketch indoor_mod (saved by Fritzing 0.8.5b)
breadboards: 1

parts:
  Part1 = Photon
  AM1 = AM2302 Humidity and Temperature Sensor
  LED1 = LED - 5mm [color="Red (633nm)" package="5 mm [THT]"]
  R1 = Resistor [tolerance=±5% resistance=220 package=THT]
  LED2 = LED - 5mm [color="Green (555nm)" package="5 mm [THT]"]
  R2 = Resistor [tolerance=±5% resistance=220 package=THT]

nets:
  GND: Part1.GND, AM1.GND, LED1.cathode
  N1: Part1.D0, R1.Pin_0
  N2: Part1.D1, AM1.DATA
  3V3: Part1.3V3, AM1.VDD, R2.Pin_0
  N3: LED1.anode, R2.Pin_1
  N4: R1.Pin_1, LED2.anode
